// Logisim project cpu.circ as structural Verilog: 1 circuit, main circuit cpu
module cpu (
  input  clk,
  input  [31:0] Instruction,
  input  [31:0] MemReadData,
  output [31:0] MemAddress,
  output [31:0] ProgramCounter,
  output [31:0] ra,
  output [31:0] sp,
  output [31:0] t0,
  output [31:0] t1,
  output [31:0] t2,
  output [31:0] s0,
  output [31:0] s1,
  output [31:0] a0,
  output [3:0] MemWriteMask,
  output [31:0] MemWriteData
);

  wire BSel, partial_store_1_p1, partial_store_1_p2, partial_store_1_p4, partial_store_1_p6, RegWEn;
  wire [2:0] ImmSel;
  wire [3:0] ALUSel;
  wire [31:0] adder_1_out, Immediate, multiplexer_1_out, RegWrite, RRD1, RRD2;

  Register #(.width(32)) PC (.D(adder_1_out), .clk(clk), .Q(ProgramCounter));  // open: en, clr
  Adder #(.width(32)) adder_1 (.a(ProgramCounter), .b(32'h4), .out(adder_1_out));  // open: cin, cout
  control_logic control_logic_1 (
    .RegWEn(RegWEn), .ImmSel(ImmSel), .BSel(BSel), .ALUSel(ALUSel),
    .Instruction({Instruction[31:20], Instruction[24:20], Instruction[14:0]}));  // open: PCSel, BrUn, ASel, MemWEn, WBSel, BrEq, BrLt
  regfile regfile_1 (
    .ReadReg1(Instruction[24:20]), .ReadReg2(Instruction[24:20]), .WriteReg(Instruction[11:7]),
    .RegWriteData(RegWrite), .RegWEn(RegWEn), .clk(clk), .ra(ra), .sp(sp), .t0(t0), .t1(t1), .t2(t2),
    .s0(s0), .s1(s1), .a0(a0), .RegReadData1(RRD1), .RegReadData2(RRD2));
  imm_gen imm_gen_1 (
    .Instruction({Instruction[31:20], Instruction[24:20], Instruction[14:0]}), .ImmSel(ImmSel),
    .Immediate(Immediate));
  Multiplexer #(.width(32)) multiplexer_1 (
    .in0(RRD2), .in1(Immediate), .out(multiplexer_1_out), .sel(BSel));  // open: en
  alu alu_1 (.ALUResult(RegWrite), .A(RRD1), .B(multiplexer_1_out), .ALUSel(ALUSel));
  // branch_comp branch_comp_1: pin names not known
  // partial_store partial_store_1: pin names not known; wires that end beside it: partial_store_1_p1, partial_store_1_p2, partial_store_1_p2, partial_store_1_p4, partial_store_1_p4, partial_store_1_p6, partial_store_1_p1, partial_store_1_p6
  // partial_load partial_load_1: pin names not known

  assign Instruction[19:15] = Instruction[24:20];

  // Other names for the same wires on the sheet: rd[4:0] = Instruction[11:7]; rs1[4:0] = Instruction[24:20]

  // Notes on the sheet:
  //   To IMEM
  //   IMEM (do **NOT** move this)
  //   From IMEM
  //   Inputs/Outputs for testing. Do **NOT** move these.
  //   It is OK to move the PC, RegFile, ALU, MEM, Branch Comp, Imm Gen, Partial Load, Partial Store and Control Logic to wherever is most convenient for you when constructing your CPU, and to delete this text
  //   To DMEM
  //   DMEM (do **NOT** move this)
  //   From DMEM
endmodule
