// Logisim project regfile.circ as structural Verilog: 1 circuit, main circuit regfile
module regfile (
  input  [4:0] ReadReg1,
  input  [4:0] ReadReg2,
  input  [4:0] WriteReg,
  input  [31:0] RegWriteData,
  input  RegWEn,
  input  clk,
  output [31:0] ra,
  output [31:0] sp,
  output [31:0] t0,
  output [31:0] t1,
  output [31:0] t2,
  output [31:0] s0,
  output [31:0] s1,
  output [31:0] a0,
  output [31:0] RegReadData1,
  output [31:0] RegReadData2
);

  wire WE1, WE2, WE3, WE4, WE5, WE6, WE7, WE8, WE9, WE10, WE11, WE12, WE13, WE14, WE15, WE16, WE17, WE18,
       WE19, WE20, WE21, WE22, WE23, WE24, WE25, WE26, WE27, WE28, WE29, WE30, WE31;
  wire [31:0] x3, x4, x11, x12, x13, x14, x15, x16, x17, x18, x19, x20, x21, x22, x23, x24, x25, x26, x27,
       x28, x29, x30, x31;

  Register #(.width(32)) register_1 (.D(RegWriteData), .en(WE8), .clk(clk), .Q(s0));  // open: clr
  Register #(.width(32)) register_2 (.D(RegWriteData), .en(WE16), .clk(clk), .Q(x16));  // open: clr
  Register #(.width(32)) register_3 (.D(RegWriteData), .en(WE25), .clk(clk), .Q(x25));  // open: clr
  Multiplexer #(.enable("false"), .select(5), .width(32)) multiplexer_1 (
    .in0({32{1'b0}}), .in1(ra), .in2(sp), .in3(x3), .in4(x4), .in5(t0), .in6(t1), .in7(t2), .in8(s0),
    .in9(s1), .in10(a0), .in11(x11), .in12(x12), .in13(x13), .in14(x14), .in15(x15), .in16(x16), .in17(x17),
    .in18(x18), .in19(x19), .in20(x20), .in21(x21), .in22(x22), .in23(x23), .in24(x24), .in25(x25),
    .in26(x26), .in27(x27), .in28(x28), .in29(x29), .in30(x30), .in31(x31), .out(RegReadData1), .sel(ReadReg1));
  Register #(.width(32)) register_4 (.D(RegWriteData), .en(WE1), .clk(clk), .Q(ra));  // open: clr
  Register #(.width(32)) register_5 (.D(RegWriteData), .en(WE9), .clk(clk), .Q(s1));  // open: clr
  Register #(.width(32)) register_6 (.D(RegWriteData), .en(WE17), .clk(clk), .Q(x17));  // open: clr
  Register #(.width(32)) register_7 (.D(RegWriteData), .en(WE26), .clk(clk), .Q(x26));  // open: clr
  Register #(.width(32)) register_8 (.D(RegWriteData), .en(WE17), .clk(clk), .Q(x18));  // open: clr
  Register #(.width(32)) register_9 (.D(RegWriteData), .en(WE2), .clk(clk), .Q(sp));  // open: clr
  Register #(.width(32)) register_10 (.D(RegWriteData), .en(WE10), .clk(clk), .Q(a0));  // open: clr
  Register #(.width(32)) register_11 (.D(RegWriteData), .en(WE18), .clk(clk), .Q(x19));  // open: clr
  Register #(.width(32)) register_12 (.D(RegWriteData), .en(WE27), .clk(clk), .Q(x27));  // open: clr
  Register #(.width(32)) register_13 (.D(RegWriteData), .en(WE3), .clk(clk), .Q(x3));  // open: clr
  Register #(.width(32)) register_14 (.D(RegWriteData), .en(WE11), .clk(clk), .Q(x11));  // open: clr
  Register #(.width(32)) register_15 (.D(RegWriteData), .en(WE20), .clk(clk), .Q(x20));  // open: clr
  Register #(.width(32)) register_16 (.D(RegWriteData), .en(WE28), .clk(clk), .Q(x28));  // open: clr
  Register #(.width(32)) register_17 (.D(RegWriteData), .en(WE4), .clk(clk), .Q(x4));  // open: clr
  Register #(.width(32)) register_18 (.D(RegWriteData), .en(WE12), .clk(clk), .Q(x12));  // open: clr
  Register #(.width(32)) register_19 (.D(RegWriteData), .en(WE21), .clk(clk), .Q(x21));  // open: clr
  Multiplexer #(.enable("false"), .select(5), .width(32)) multiplexer_2 (
    .in0({32{1'b0}}), .in1(ra), .in2(sp), .in3(x3), .in4(x4), .in5(t0), .in6(t1), .in7(t2), .in8(s0),
    .in9(s1), .in10(a0), .in11(x11), .in12(x12), .in13(x13), .in14(x14), .in15(x15), .in16(x16), .in17(x17),
    .in18(x18), .in19(x19), .in20(x20), .in21(x21), .in22(x22), .in23(x23), .in24(x24), .in25(x25),
    .in26(x26), .in27(x27), .in28(x28), .in29(x29), .in30(x30), .in31(x31), .out(RegReadData2), .sel(ReadReg2));
  Register #(.width(32)) register_20 (.D(RegWriteData), .en(WE5), .clk(clk), .Q(t0));  // open: clr
  Register #(.width(32)) register_21 (.D(RegWriteData), .en(WE13), .clk(clk), .Q(x13));  // open: clr
  Register #(.width(32)) register_22 (.D(RegWriteData), .en(WE22), .clk(clk), .Q(x22));  // open: clr
  Register #(.width(32)) register_23 (.D(RegWriteData), .en(WE29), .clk(clk), .Q(x29));  // open: clr
  Register #(.width(32)) register_24 (.D(RegWriteData), .en(WE6), .clk(clk), .Q(t1));  // open: clr
  Register #(.width(32)) register_25 (.D(RegWriteData), .en(WE14), .clk(clk), .Q(x14));  // open: clr
  Register #(.width(32)) register_26 (.D(RegWriteData), .en(WE23), .clk(clk), .Q(x23));  // open: clr
  Register #(.width(32)) register_27 (.D(RegWriteData), .en(WE30), .clk(clk), .Q(x30));  // open: clr
  Demultiplexer #(.enable("false"), .select(5)) demultiplexer_1 (
    .out1(WE1), .out2(WE2), .out3(WE3), .out4(WE4), .out5(WE5), .out6(WE6), .out7(WE7), .out8(WE8),
    .out9(WE9), .out10(WE10), .out11(WE11), .out12(WE12), .out13(WE13), .out14(WE14), .out15(WE15),
    .out16(WE16), .out17(WE17), .out18(WE18), .out19(WE19), .out20(WE20), .out21(WE21), .out22(WE22),
    .out23(WE23), .out24(WE24), .out25(WE25), .out26(WE26), .out27(WE27), .out28(WE28), .out29(WE29),
    .out30(WE30), .out31(WE31), .in(RegWEn), .sel(WriteReg));  // open: out0
  Register #(.width(32)) register_28 (.D(RegWriteData), .en(WE7), .clk(clk), .Q(t2));  // open: clr
  Register #(.width(32)) register_29 (.D(RegWriteData), .en(WE15), .clk(clk), .Q(x15));  // open: clr
  Register #(.width(32)) register_30 (.D(RegWriteData), .en(WE24), .clk(clk), .Q(x24));  // open: clr
  Register #(.width(32)) register_31 (.D(RegWriteData), .en(WE31), .clk(clk), .Q(x31));  // open: clr

  // Other names for the same wires on the sheet: x1[31:0] = ra; x2[31:0] = sp; x5[31:0] = t0; x6[31:0] = t1;
  //   x7[31:0] = t2; x8[31:0] = s0; x9[31:0] = s1; x10[31:0] = a0

  // Notes on the sheet:
  //   INPUTS to your circuit
  //   DON'T CHANGE THE LOCATIONS OF THE INPUTS AND OUTPUTS!
  //   These are DEBUG/TEST outputs from your circuit.
  //   OUTPUTS from your circuit
endmodule
